# Fritzing sketch big-lantern (saved by Fritzing 0.9.3b)
perfboards: 1

parts:
  BAT1 = Battery Holders [package=battcom_20mm_pth]
  BAT2 = Battery Holders [package=battcom_20mm_pth]
  U1 = attiny85 [package=dip]
  S1 = Reed switch [package=THT]
  R1 = Resistor [tolerance=±5% resistance=10 package=THT]
  LED4 = LED - 5mm [color="White (4500K)" package="5 mm [THT]"]
  LED5 = LED - 5mm [color="White (4500K)" package="5 mm [THT]"]

nets:
  N1: BAT1.+, BAT2.+
  N2: BAT1.-, BAT2.-, R1.Pin_0
  N3: U1.Pin_4, S1.pin_1
  N4: U1.Pin_5, LED4.anode, LED5.anode
  N5: U1.Pin_7, S1.pin_2
  N6: R1.Pin_1, LED4.cathode, LED5.cathode

notes:
  White band wires run under board
  Grey is solder
