# Fritzing sketch schematic (saved by Fritzing 0.9.3b)
breadboards: 1

parts:
  BAT1 = Battery Holders [package=battcom_20mm_pth]
  U1 = attiny85 [package=dip]
  LED1 = LEDs [package=led10mm]
  R1 = Resistor [tolerance=±5% resistance=220 package=THT]
  S1 = Reed switch [package=THT]

nets:
  N1: BAT1.+, U1.Pin_8
  N2: BAT1.-, U1.Pin_4, LED1.A, S1.pin_1
  N3: U1.Pin_5, R1.Pin_0
  N4: U1.Pin_7, S1.pin_2
  N5: LED1.C, R1.Pin_1
