# Fritzing sketch small-lantern (saved by Fritzing 0.9.3b)
perfboards: 1

parts:
  U1 = attiny85 [package=dip]
  S1 = Reed switch [package=THT]
  R1 = Resistor [tolerance=±5% resistance=10 package=THT]
  BAT2 = Battery Holders [package=battcom_20mm_pth]
  LED5 = LED - 5mm [color="White (4500K)" package="5 mm [THT]"]

nets:
  N1: U1.Pin_4, S1.pin_2
  N2: U1.Pin_5, LED5.anode
  N3: U1.Pin_7, S1.pin_1
  N4: U1.Pin_8, BAT2.+
  N5: R1.Pin_0, BAT2.-
  N6: R1.Pin_1, LED5.cathode

notes:
  White band wires run under board
  Grey is solder
